# Fritzing sketch CWKeyer (saved by Fritzing 1.0.4)
circuit board: 8.43632cm x 6.50662cm
breadboards: 1

parts:
  ESP8266 = NodeMCU V3.0
  Battery = male pin header, 2 pins [form="♂ (male)"]
  Buzz = Piezo Speaker
  Display = male pin header, 4 pins [form="♂ (male)"]
  Volume = 6mm Trimmer Potentiometer [maximum_resistance=10kΩ knob_status=50% power=0.5W package=THT]
  UART = male pin header, 4 pins [form="♂ (male)"]
  Speaker = 3.5mm Audio Jack [package=audio-jack]
  Key = 3.5mm Audio Jack [package=audio-jack]
  RE1 = KY-040 Rotary encoder [package="Breakout board"]

nets:
  N1: ESP8266.D1, Display.pin3
  N2: ESP8266.D2, Display.pin4
  3V3: ESP8266.3V3, Display.pin2, UART.pin2, RE1.Vcc
  GND: ESP8266.GND, Battery.pin2, Buzz.pin2, Display.pin1, Volume.leg1, UART.pin1, Speaker.SLEEVE, Key.SLEEVE, RE1.GND
  N3: ESP8266.D5, Volume.leg2
  N4: ESP8266.D6, Key.LEFT
  N5: ESP8266.D7, Key.RIGHT
  N6: ESP8266.D8, Buzz.pin1
  N7: ESP8266.RX, UART.pin3
  N8: ESP8266.TX, UART.pin4
  N9: ESP8266.Vin, Battery.pin1
  N10: Volume.wiper, Speaker.RIGHT, Speaker.LEFT

notes:
  DL1SKD
  CWKeyer
  Ver 0.5

custom parts:
  NodeMCU V3.0: ESP8266 based NodeMCU
  KY-040 Rotary encoder: KY-040 Rotary Encoder with switch on breakout borad from AZ Delivery
